# Fritzing sketch attiny-programmer_switch (saved by Fritzing 0.9.3b)
circuit board: 3.41208cm x 5.19888cm
breadboards: 1

parts:
  C2 = Electrolytic Capacitor [capacitance=1µF package="100 mil [THT, electrolytic]"]
  attiny86 = attiny85 [package=dip]
  attiny85_programmer = Arduino Uno (Rev3)
  Q1 = TRANSISTOR_NPN [package=sot23-3]
  J1 = female pin header, 4 pins [form="♀ (female)"]
  J2 = female pin header, 4 pins [form="♀ (female)"]
  Q2 = TRANSISTOR_NPN [package=sot23-3]

nets:
  N1: C2.-, attiny86.Pin_4, attiny85_programmer.GND, Q1.E, J1.pin2, Q2.E
  N2: C2.+, attiny85_programmer.RESET
  N3: attiny86.Pin_1, attiny85_programmer.D10_PWM/SS, J2.pin4
  N4: attiny86.Pin_2, Q1.C, J1.pin4
  N5: attiny86.Pin_3, J1.pin3, Q2.C
  N6: attiny86.Pin_5, attiny85_programmer.D11_PWM/MOSI, J2.pin1
  N7: attiny86.Pin_6, attiny85_programmer.D12/MISO, J2.pin2
  N8: attiny86.Pin_7, attiny85_programmer.D13/SCK, J2.pin3
  N9: attiny86.Pin_8, attiny85_programmer.5V, J1.pin1

notes:
  ATtiny85
  10 micro
  tested with Arduino IDE 1.5.6-r2
  +
  3
  0
  1
  rst
  -
  A3P3
  A2P4
  P1
  P0
  A1P2
  gnd
  4
  3 A3
  4 A2
  2 A1
