# Fritzing sketch attiny-programmer (saved by Fritzing 0.9.3b)
circuit board: 2.84052cm x 5.15623cm
breadboards: 1

parts:
  C2 = Electrolytic Capacitor [capacitance=1µF package="100 mil [THT, electrolytic]"]
  J1 = female pin header, 8 pins [form="♀ (female)"]
  attiny86 = attiny85 [package=dip]
  S10 = Toggle Switch [package=THT]
  S11 = Toggle Switch [package=THT]
  S12 = Toggle Switch [package=THT]
  J2 = female pin header, 3 pins [form="♀ (female)"]
  attiny85_programmer = Arduino Uno (Rev3)
  J3 = female pin header, 3 pins [form="♀ (female)"]
  J4 = female pin header, 3 pins [form="♀ (female)"]
  J5 = female pin header, 3 pins [form="♀ (female)"]
  J6 = female pin header, 3 pins [form="♀ (female)"]

nets:
  N1: C2.-, attiny85_programmer.GND, J5.pin3
  N2: C2.+, attiny85_programmer.RESET
  N3: J1.pin1, S12.L2
  N4: J1.pin2, S11.L2
  N5: J1.pin3, S10.L2
  N6: J1.pin4, J3.pin3
  N7: J1.pin5, J2.pin1
  N8: J1.pin6, J6.pin1
  N9: J1.pin7, J4.pin1
  N10: J1.pin8, J5.pin1
  N11: attiny86.Pin_1, J2.pin2
  N12: attiny86.Pin_2, J6.pin2
  N13: attiny86.Pin_3, J4.pin2
  N14: attiny86.Pin_4, J5.pin2
  N15: attiny86.Pin_5, J3.pin2
  N16: attiny86.Pin_6, S10.COM
  N17: attiny86.Pin_7, S11.COM
  N18: attiny86.Pin_8, S12.COM
  N19: S10.L1, attiny85_programmer.D12/MISO
  N20: S11.L1, attiny85_programmer.D13/SCK
  N21: S12.L1, attiny85_programmer.5V
  N22: J2.pin3, attiny85_programmer.D10_PWM/SS
  N23: attiny85_programmer.D11_PWM/MOSI, J3.pin1

notes:
  ATtiny85
  10 micro
  tested with Arduino IDE 1.5.6-r2
  +
  2 A1
  1
  0
  rst
  gnd
  3 A3
  4 A2
  -
  3
  4
  2
